// Logisim project cpu.circ as structural Verilog: 2 circuits, main circuit main
module main (
);

  wire A_WRITE, ALU_CARRY, ALU_H_aeqb, ALU_L_aeqb, ALU_L_cn_4, ALU_MODE, ALU_S0, ALU_S1, ALU_S2, ALU_S3,
       and_1_out, and_2_out, and_3_out, and_4_out, B_WRITE, button_1_out, button_2_out, button_3_out,
       C_WRITE, CARRY, CLK, clock_1_out, comparator_2_eq, d_ff_1_q, D_WRITE, E_WRITE, END_INSTR, EQUAL,
       FLAGS_SYS_UPDATE, FLAGS_USR_UPDATE, IE_qn, IE_TOGGLE, INTERRUPT, IR_WRITE, MEM_INHIBIT, nA_OUT,
       nAH_OUT, nAL_OUT, nALU_OUT, nand_1_out, nBC_OUT, nDE_OUT, not_1_out, not_2_out, not_3_out, not_4_out,
       not_5_out, not_6_out, not_7_out, not_8_out, not_9_out, not_10_out, not_11_out, nPC_OUT, nRAM_OUT,
       nRAM_WRITE, nSP_OUT, nT_OUT, PC_H_WRITE, PC_L_WRITE, RST, SP_H_WRITE, SP_L_WRITE, T_WRITE;
  wire [3:0] STEP_q;
  wire [6:0] keyboard_1_data;
  wire [7:0] A_q, ALU_L_f0, B_q, C_q, controlled_buffer_5_out, D_q, E_q, IR_q, PC_H_q, PC_L_q, ram_1_data,
       register_1_q, register_2_q, SP_H_q, SP_L_q, T_q;
  wire [7:4] d_ff_2_q;
  wire [15:0] controlled_buffer_1_out;
  wire [31:8] rom_1_data;

  // Probe on ALU_L_f0
  Register PC_H (.D(ALU_L_f0), .en(1'b1), .clk(PC_H_WRITE), .Q(PC_H_q));  // open: clr
  Register PC_L (.D(ALU_L_f0), .en(1'b1), .clk(PC_L_WRITE), .Q(PC_L_q));  // open: clr
  Register SP_H (.D(ALU_L_f0), .en(1'b1), .clk(SP_H_WRITE), .Q(SP_H_q), .clr(RST));
  Register SP_L (.D(ALU_L_f0), .en(1'b1), .clk(SP_L_WRITE), .Q(SP_L_q), .clr(RST));
  Register B (.D(ALU_L_f0), .en(1'b1), .clk(B_WRITE), .Q(B_q), .clr(RST));
  Register C (.D(ALU_L_f0), .en(1'b1), .clk(C_WRITE), .Q(C_q), .clr(RST));
  Register D (.D(ALU_L_f0), .en(1'b1), .clk(D_WRITE), .Q(D_q), .clr(RST));
  Register E (.D(ALU_L_f0), .en(1'b1), .clk(E_WRITE), .Q(E_q), .clr(RST));
  assign controlled_buffer_1_out = not_1_out ? {PC_H_q, PC_L_q} : 16'bz;  // Controlled_Buffer controlled_buffer_1
  not not_1 (not_1_out, nPC_OUT);
  assign controlled_buffer_1_out = not_2_out ? {SP_H_q, SP_L_q} : 16'bz;  // Controlled_Buffer controlled_buffer_2
  not not_2 (not_2_out, nSP_OUT);
  assign controlled_buffer_1_out = not_3_out ? {B_q, C_q} : 16'bz;  // Controlled_Buffer controlled_buffer_3
  not not_3 (not_3_out, nBC_OUT);
  assign controlled_buffer_1_out = not_4_out ? {D_q, E_q} : 16'bz;  // Controlled_Buffer controlled_buffer_4
  Pull_Resistor pull_resistor_1 (.node(controlled_buffer_1_out));
  not not_4 (not_4_out, nDE_OUT);
  // Probe on controlled_buffer_1_out
  TTY #(.cols(64), .rows(16)) tty_1 (.data(ram_1_data[6:0]), .clk(CLK), .we(and_1_out), .clr(RST));
  Comparator #(.mode("unsigned"), .width(16)) comparator_1 (
    .a(controlled_buffer_1_out), .b(16'h7fff), .eq(MEM_INHIBIT));  // open: gt, lt
  and and_1 (and_1_out, MEM_INHIBIT, ~nRAM_WRITE);  // AND_Gate
  and and_2 (and_2_out, MEM_INHIBIT, ~nRAM_OUT);  // AND_Gate
  not not_5 (not_5_out, nAH_OUT);
  assign controlled_buffer_5_out = not_5_out ? controlled_buffer_1_out[15:8] : 8'bz;  // Controlled_Buffer controlled_buffer_5
  assign controlled_buffer_5_out = not_6_out ? controlled_buffer_1_out[7:0] : 8'bz;  // Controlled_Buffer controlled_buffer_6
  not not_6 (not_6_out, nAL_OUT);
  Comparator #(.mode("unsigned"), .width(16)) comparator_2 (
    .a(controlled_buffer_1_out), .b(16'h1d7), .eq(comparator_2_eq));  // open: gt, lt
  Button button_1 (.out(button_1_out));
  RAM #(.addrWidth(16), .databus("bidir"), .trigger("low"), .\type ("nonvolatile")) ram_1 (
    .addr(controlled_buffer_1_out), .we(nand_1_out), .oe(and_3_out), .data(ram_1_data));
  nand nand_1 (nand_1_out, ~nRAM_WRITE, ~MEM_INHIBIT);  // NAND_Gate
  and and_3 (and_3_out, ~nRAM_OUT, ~MEM_INHIBIT);  // AND_Gate
  Button button_2 (.out(button_2_out));
  D_Flip_Flop d_ff_1 (
    .D(1'b0), .clk(and_4_out), .Q(d_ff_1_q), .preset(button_2_out), .reset(button_3_out));  // open: Qn
  and and_4 (and_4_out, comparator_2_eq, button_1_out);
  Button button_3 (.out(button_3_out));
  Keyboard keyboard_1 (.clk(CLK), .re(and_2_out), .clr(RST), .avail(INTERRUPT), .data(keyboard_1_data));
  and and_5 (CLK, d_ff_1_q, clock_1_out);
  Clock clock_1 (.out(clock_1_out));
  Button button_4 (.out(RST));
  not not_7 (not_7_out, nALU_OUT);
  assign ram_1_data = not_7_out ? ALU_L_f0 : 8'bz;  // Controlled_Buffer controlled_buffer_7
  // Probe on ram_1_data
  assign ram_1_data = and_2_out ? {1'b0, keyboard_1_data} : 8'bz;  // Controlled_Buffer controlled_buffer_8
  Pull_Resistor pull_resistor_2 (.node(ram_1_data));
  // Probe on ALU_L_f0
  D_Flip_Flop d_ff_2 (.D(CARRY), .clk(FLAGS_USR_UPDATE), .Q(d_ff_2_q[4]));  // open: Qn, preset, reset
  D_Flip_Flop d_ff_3 (.D(EQUAL), .clk(FLAGS_USR_UPDATE), .Q(d_ff_2_q[5]));  // open: Qn, preset, reset
  D_Flip_Flop d_ff_4 (.D(CARRY), .clk(FLAGS_SYS_UPDATE), .Q(d_ff_2_q[6]));  // open: Qn, preset, reset
  D_Flip_Flop d_ff_5 (.D(INTERRUPT), .clk(END_INSTR), .Q(d_ff_2_q[7]), .reset(IE_qn));  // open: Qn, preset
  D_Flip_Flop IE (.D(IE_qn), .clk(IE_TOGGLE), .Qn(IE_qn), .reset(RST));  // open: Q, preset
  Register IR (.D(ram_1_data), .clk(IR_WRITE), .Q(IR_q), .clr(RST));  // open: en
  Register A (.D(ALU_L_f0), .clk(A_WRITE), .Q(A_q), .clr(RST));  // open: en
  Register T (.D(ALU_L_f0), .clk(T_WRITE), .Q(T_q), .clr(RST));  // open: en
  Counter #(.max('hf), .width(4)) STEP (
    .load(RST), .D(4'b0000), .count(1'b1), .Q(STEP_q), .clk(CLK), .clr(END_INSTR));  // open: carry, up
  Register #(.trigger("high")) register_1 (.D({d_ff_2_q, STEP_q}), .clk(CLK), .Q(register_1_q));  // open: en, clr
  Register #(.trigger("high")) register_2 (.D(IR_q), .clk(CLK), .Q(register_2_q));  // open: en, clr
  assign controlled_buffer_5_out = not_8_out ? A_q : 8'bz;  // Controlled_Buffer controlled_buffer_9
  not not_8 (not_8_out, nA_OUT);
  Pull_Resistor pull_resistor_3 (.node(controlled_buffer_5_out));
  assign ram_1_data = not_9_out ? T_q : 8'bz;  // Controlled_Buffer controlled_buffer_10
  not not_9 (not_9_out, nT_OUT);
  // Probe on controlled_buffer_5_out
  // Probe on ram_1_data
  ROM #(.addrWidth(16), .dataWidth(32)) rom_1 (
    .addr({register_2_q, register_1_q}),
    .data({rom_1_data[31:24], ALU_S3, ALU_S2, ALU_S1, ALU_S0, ALU_CARRY, nAL_OUT, ALU_MODE, nAH_OUT, rom_1_data[15:8], nRAM_OUT, nDE_OUT, nBC_OUT, nT_OUT, nA_OUT, nPC_OUT, nALU_OUT, nSP_OUT}));
  alu_74181 ALU_H (
    .B0(ram_1_data[4]), .A0(controlled_buffer_5_out[4]), .M(ALU_MODE), .Cn(ALU_L_cn_4), .S3(ALU_S3),
    .S2(ALU_S2), .S1(ALU_S1), .S0(ALU_S0), .B3(ram_1_data[7]), .A3(controlled_buffer_5_out[7]),
    .B2(ram_1_data[6]), .A2(controlled_buffer_5_out[6]), .B1(ram_1_data[5]), .A1(controlled_buffer_5_out[5]),
    .F1(ALU_L_f0[5]), .F0(ALU_L_f0[4]), .Cn_4(CARRY), .F3(ALU_L_f0[7]), .F2(ALU_L_f0[6]), .AeqB(ALU_H_aeqb));  // open: G, P
  alu_74181 ALU_L (
    .B0(ram_1_data[0]), .A0(controlled_buffer_5_out[0]), .M(ALU_MODE), .Cn(ALU_CARRY), .S3(ALU_S3),
    .S2(ALU_S2), .S1(ALU_S1), .S0(ALU_S0), .B3(ram_1_data[3]), .A3(controlled_buffer_5_out[3]),
    .B2(ram_1_data[2]), .A2(controlled_buffer_5_out[2]), .B1(ram_1_data[1]), .A1(controlled_buffer_5_out[1]),
    .F1(ALU_L_f0[1]), .F0(ALU_L_f0[0]), .Cn_4(ALU_L_cn_4), .F3(ALU_L_f0[3]), .F2(ALU_L_f0[2]),
    .AeqB(ALU_L_aeqb));  // open: G, P
  and and_6 (EQUAL, ALU_H_aeqb, ALU_L_aeqb);
  not not_10 (not_10_out, CLK);
  not not_11 (not_11_out, CLK);
  assign {D_WRITE, E_WRITE, SP_L_WRITE, C_WRITE, PC_L_WRITE, B_WRITE, SP_H_WRITE, PC_H_WRITE} = not_10_out ? rom_1_data[15:8] : 8'bz;  // Controlled_Buffer controlled_buffer_11
  Pull_Resistor pull_resistor_4 (.node(PC_H_WRITE));
  assign {FLAGS_SYS_UPDATE, FLAGS_USR_UPDATE, IR_WRITE, IE_TOGGLE, END_INSTR, nRAM_WRITE, T_WRITE, A_WRITE} = not_11_out ? rom_1_data[31:24] : 8'bz;  // Controlled_Buffer controlled_buffer_12
  Pull_Resistor pull_resistor_5 (.node(A_WRITE));
  Pull_Resistor pull_resistor_6 (.node(SP_H_WRITE));
  Pull_Resistor pull_resistor_7 (.node(B_WRITE));
  Pull_Resistor pull_resistor_8 (.node(PC_L_WRITE));
  Pull_Resistor pull_resistor_9 (.node(C_WRITE));
  Pull_Resistor #(.pull(1)) pull_resistor_10 (.node(nRAM_WRITE));
  Pull_Resistor pull_resistor_11 (.node(T_WRITE));
  Pull_Resistor pull_resistor_12 (.node(END_INSTR));
  Pull_Resistor pull_resistor_13 (.node(IE_TOGGLE));
  Pull_Resistor pull_resistor_14 (.node(SP_L_WRITE));
  Pull_Resistor pull_resistor_15 (.node(E_WRITE));
  Pull_Resistor pull_resistor_16 (.node(D_WRITE));
  Pull_Resistor pull_resistor_17 (.node(IR_WRITE));
  Pull_Resistor pull_resistor_18 (.node(FLAGS_USR_UPDATE));
  Pull_Resistor pull_resistor_19 (.node(FLAGS_SYS_UPDATE));

  // Notes on the sheet:
  //   contents of rom_1 (hex, n*v repeats v):
  //   437087b 405017b 2c05007b 13*c0500ff 437087b 405017b 2c05007b 13*c0500ff 437087b 405017b 2c05007b
  //   13*c0500ff 437087b 405017b 2c05007b 13*c0500ff 437087b 405017b 2c05007b 13*c0500ff 437087b 405017b
  //   2c05007b 13*c0500ff 437087b 405017b 2c05007b 13*c0500ff 437087b 405017b 2c05007b 13*c0500ff 84f920fe
  //   40c02fe 60900fb 500ee 84f920fe 40c02fe 60c00fb 500ee 437087b 1c37017e 6*c0500ff 84f920fe 40c02fe
  //   60900fb 500ee 84f920fe 40c02fe 60c00fb 500ee 437087b 1c37017e 6*c0500ff 84f920fe 40c02fe 60900fb
  //   500ee 84f920fe 40c02fe 60c00fb 500ee 437087b 1c37017e 6*c0500ff 84f920fe 40c02fe 60900fb 500ee
  //   84f920fe 40c02fe 60c00fb 500ee 437087b 1c37017e 6*c0500ff 84f920fe 4fc02fe 60900fb 500ee 84f920fe
  //   4fc02fe 60c00fb 500ee 437087b 1c37017e 6*c0500ff 84f920fe 4fc02fe 60900fb 500ee 84f920fe 4fc02fe
  //   60c00fb 500ee 437087b 1c37017e 6*c0500ff 84f920fe 4fc02fe 60900fb 500ee 84f920fe 4fc02fe 60c00fb
  //   500ee 437087b 1c37017e 6*c0500ff 84f920fe 4fc02fe 60900fb 500ee 84f920fe 4fc02fe 60c00fb 500ee
  //   437087b 1c37017e 6*c0500ff a401087b 40401fb 5a7007b 840108fb c0401fb 11*c0500ff a401087b 40401fb
  //   5a7007b 840108fb c0401fb 11*c0500ff a401087b 40401fb 5a7007b 840108fb c0401fb 11*c0500ff a401087b
  //   40401fb 5a7007b 840108fb c0401fb 11*c0500ff a401087b 40c01fb 5a7007b 840108fb c0c01fb 11*c0500ff
  //   a401087b 40c01fb 5a7007b 840108fb c0c01fb 11*c0500ff a401087b 40c01fb 5a7007b 840108fb c0c01fb
  //   11*c0500ff a401087b 40c01fb 5a7007b 840108fb c0c01fb 11*c0500ff 84f920fe 40c02fe 60900fb 500ee
  //   84f920fe 40c02fe 60c00fb 500ee 437087b 1c37017e 6*c0500ff 84f920fe 40c02fe 60900fb 500ee 84f920fe
  //   40c02fe 60c00fb 500ee 437087b 1c37017e 6*c0500ff 84f920fe 40c02fe 60900fb 500ee 84f920fe 40c02fe
  //   60c00fb 500ee 437087b 1c37017e 6*c0500ff 84f920fe 40c02fe 60900fb 500ee 84f920fe 40c02fe 60c00fb
  //   500ee 437087b 1c37017e 6*c0500ff 84f920fe 4fc02fe 60900fb 500ee 84f920fe 4fc02fe 60c00fb 500ee
  //   437087b 1c37017e 6*c0500ff 84f920fe 4fc02fe 60900fb 500ee 84f920fe 4fc02fe 60c00fb 500ee 437087b
  //   1c37017e 6*c0500ff 84f920fe 4fc02fe 60900fb 500ee 84f920fe 4fc02fe 60c00fb 500ee 437087b 1c37017e
  //   6*c0500ff 84f920fe 4fc02fe 60900fb 500ee 84f920fe 4fc02fe 60c00fb 500ee 437087b 1c37017e 6*c0500ff
  //   a401087b 40401fb 4a7047b 840108fb c0401fb 11*c0500ff a401087b 40401fb 4a7047b 840108fb c0401fb
  //   11*c0500ff a401087b 40401fb 4a7047b 840108fb c0401fb 11*c0500ff a401087b 40401fb 4a7047b 840108fb
  //   c0401fb 11*c0500ff a401087b 40c01fb 4a7047b 840108fb c0c01fb 11*c0500ff a401087b 40c01fb 4a7047b
  //   840108fb c0c01fb 11*c0500ff a401087b 40c01fb 4a7047b 840108fb c0c01fb 11*c0500ff a401087b 40c01fb
  //   4a7047b 840108fb c0c01fb 11*c0500ff 84f920fe 40c02fe 60900fb 500ee 84f920fe 40c02fe 60c00fb 500ee
  //   437087b 1c37017e 6*c0500ff 84f920fe 40c02fe 60900fb 500ee 84f920fe 40c02fe 60c00fb 500ee 437087b
  //   1c37017e 6*c0500ff 84f920fe 40c02fe 60900fb 500ee 84f920fe 40c02fe 60c00fb 500ee 437087b 1c37017e
  //   6*c0500ff 84f920fe 40c02fe 60900fb 500ee 84f920fe 40c02fe 60c00fb 500ee 437087b 1c37017e 6*c0500ff
  //   84f920fe 4fc02fe 60900fb 500ee 84f920fe 4fc02fe 60c00fb 500ee 437087b 1c37017e 6*c0500ff 84f920fe
  //   4fc02fe 60900fb 500ee 84f920fe 4fc02fe 60c00fb 500ee 437087b 1c37017e 6*c0500ff 84f920fe 4fc02fe
  //   60900fb 500ee 84f920fe 4fc02fe 60c00fb 500ee 437087b 1c37017e 6*c0500ff 84f920fe 4fc02fe 60900fb
  //   500ee 84f920fe 4fc02fe 60c00fb 500ee 437087b 1c37017e 6*c0500ff a401087b 40401fb 4a7107b 840108fb
  //   c0401fb 11*c0500ff a401087b 40401fb 4a7107b 840108fb c0401fb 11*c0500ff a401087b 40401fb 4a7107b
  //   840108fb c0401fb 11*c0500ff a401087b 40401fb 4a7107b 840108fb c0401fb 11*c0500ff a401087b 40c01fb
  //   4a7107b 840108fb c0c01fb 11*c0500ff a401087b 40c01fb 4a7107b 840108fb c0c01fb 11*c0500ff a401087b
  //   40c01fb 4a7107b 840108fb c0c01fb 11*c0500ff a401087b 40c01fb 4a7107b 840108fb c0c01fb 11*c0500ff
  //   84f920fe 40c02fe 60900fb 500ee 84f920fe 40c02fe 60c00fb 500ee 437087b 1c37017e 6*c0500ff 84f920fe
  //   40c02fe 60900fb 500ee 84f920fe 40c02fe 60c00fb 500ee 437087b 1c37017e 6*c0500ff 84f920fe 40c02fe
  //   60900fb 500ee 84f920fe 40c02fe 60c00fb 500ee 437087b 1c37017e 6*c0500ff 84f920fe 40c02fe 60900fb
  //   500ee 84f920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
  //   EEROM A
  //   EEROM C
  //   Write on clock falling edge
  //   EEROM B
  //   EEROM D
endmodule

module alu_74181 (
  input  S3,
  input  S2,
  input  S1,
  input  S0,
  input  B3,
  input  A3,
  input  B2,
  input  A2,
  input  B1,
  input  A1,
  input  B0,
  input  A0,
  input  M,
  input  Cn,
  output G,
  output Cn_4,
  output P,
  output F3,
  output F2,
  output AeqB,
  output F1,
  output F0
);

  wire and_1_out, and_2_out, and_3_out, and_4_out, and_5_out, and_6_out, and_7_out, and_8_out, and_9_out,
       and_10_out, and_11_out, and_12_out, and_13_out, and_14_out, and_15_out, and_16_out, and_17_out,
       and_18_out, and_19_out, and_20_out, and_21_out, and_22_out, and_23_out, and_24_out, and_25_out,
       and_26_out, and_28_out, and_29_out, and_30_out, and_31_out, and_32_out, and_33_out, and_34_out,
       and_35_out, and_36_out, and_37_out, and_38_out, nand_2_out, nand_4_out, nor_2_out, nor_3_out,
       nor_4_out, nor_5_out, nor_6_out, nor_7_out, nor_8_out, nor_9_out, nor_10_out, nor_11_out, nor_12_out,
       not_1_out, not_2_out, not_3_out, not_4_out, not_5_out, not_6_out, not_7_out, not_8_out, not_9_out;

  and and_1 (and_1_out, nor_3_out, nor_3_out);
  nor nor_1 (G, and_1_out, and_2_out, and_3_out, and_5_out, and_5_out);
  and and_2 (and_2_out, nor_2_out, nor_6_out);
  and and_3 (and_3_out, nor_2_out, nor_4_out, nor_9_out);
  and and_4 (and_4_out, B3, S3, A3);
  and and_5 (and_5_out, nor_2_out, nor_4_out, nor_7_out, nor_12_out, nor_12_out);
  nor nor_2 (nor_2_out, and_4_out, and_6_out);
  and and_6 (and_6_out, A3, S2, not_1_out);
  not not_1 (not_1_out, B3);
  nand nand_1 (Cn_4, G, nand_2_out);
  nand nand_2 (nand_2_out, nor_2_out, nor_4_out, nor_7_out, nor_11_out, Cn);
  nand nand_3 (P, nor_2_out, nor_4_out, nor_7_out, nor_11_out, nor_11_out);
  nor nor_3 (nor_3_out, and_7_out, and_8_out, and_10_out);
  and and_7 (and_7_out, not_1_out, S1);
  and and_8 (and_8_out, S0, B3);
  and and_9 (and_9_out, nor_2_out, not_2_out);
  and and_10 (and_10_out, A3, A3);
  and and_11 (and_11_out, nor_4_out, nor_7_out, nor_11_out, Cn, not_9_out);
  not not_2 (not_2_out, nor_3_out);
  nor nor_4 (nor_4_out, and_12_out, and_13_out);
  and and_12 (and_12_out, B2, S3, A2);
  and and_13 (and_13_out, A2, S2, not_3_out);
  xor xor_1 (F3, and_9_out, nor_5_out);
  nor nor_5 (nor_5_out, and_11_out, and_14_out, and_15_out, and_17_out, and_17_out);
  and and_14 (and_14_out, nor_4_out, nor_7_out, nor_12_out, not_9_out, not_9_out);
  and and_15 (and_15_out, nor_4_out, nor_9_out, not_9_out);
  and and_16 (and_16_out, not_3_out, S1);
  not not_3 (not_3_out, B2);
  and and_17 (and_17_out, nor_6_out, not_9_out);
  nor nor_6 (nor_6_out, and_16_out, and_18_out, and_19_out);
  and and_18 (and_18_out, S0, B2);
  and and_19 (and_19_out, A2, A2);
  and and_20 (and_20_out, nor_4_out, not_4_out);
  and and_21 (and_21_out, nor_7_out, nor_7_out, nor_11_out, Cn, not_9_out);
  not not_4 (not_4_out, nor_6_out);
  nor nor_7 (nor_7_out, and_22_out, and_25_out);
  and and_22 (and_22_out, B1, S3, A1);
  xor xor_2 (F2, and_20_out, nor_8_out);
  nor nor_8 (nor_8_out, and_21_out, and_23_out, and_24_out);
  and and_23 (and_23_out, nor_7_out, nor_12_out, not_9_out);
  and and_24 (and_24_out, nor_9_out, not_9_out);
  and and_25 (and_25_out, A1, S2, not_5_out);
  and and_26 (and_26_out, not_5_out, S1);
  not not_5 (not_5_out, B1);
  and and_27 (AeqB, F3, F3, F2, F1, F0);
  and and_28 (and_28_out, nor_7_out, not_6_out);
  not not_6 (not_6_out, nor_9_out);
  nor nor_9 (nor_9_out, and_26_out, and_29_out, and_30_out);
  and and_29 (and_29_out, S0, B1);
  and and_30 (and_30_out, A1, A1);
  and and_31 (and_31_out, Cn, nor_11_out, not_9_out);
  and and_32 (and_32_out, B0, S3, A0);
  xor xor_3 (F1, and_28_out, nor_10_out);
  nor nor_10 (nor_10_out, and_31_out, and_33_out);
  and and_33 (and_33_out, nor_12_out, not_9_out);
  nor nor_11 (nor_11_out, and_32_out, and_34_out);
  and and_34 (and_34_out, A0, S2, not_7_out);
  not not_7 (not_7_out, B0);
  and and_35 (and_35_out, nor_11_out, not_8_out);
  not not_8 (not_8_out, nor_12_out);
  nor nor_12 (nor_12_out, and_36_out, and_37_out, and_38_out);
  and and_36 (and_36_out, not_7_out, S1);
  and and_37 (and_37_out, S0, B0);
  xor xor_4 (F0, and_35_out, nand_4_out);
  nand nand_4 (nand_4_out, not_9_out, Cn);
  and and_38 (and_38_out, A0, A0);
  not not_9 (not_9_out, M);
endmodule
